# Fritzing sketch rabbitSchematic (saved by Fritzing 0.9.0b)
breadboards: 1

parts:
  Part2 = Arduino Uno (Rev3)
  J4 = Basic Servo
  S1 = Pushbutton [package="[THT]"]
  R1 = Rotary Potentiometer (Small) [maximum_resistance=100kΩ package=THT]
  S2 = Pushbutton [package="[THT]"]
  R2 = Resistor [tolerance=±5% resistance=220 package=THT]
  R3 = Resistor [tolerance=±5% resistance=220 package=THT]
  R4 = Resistor [tolerance=±5% resistance=220 package=THT]
  J5 = Piezo Speaker  # not connected
  VCC1 = Battery

nets:
  N1: Part2.A0, R1.wiper
  N2: Part2.D8, R2.Pin_0
  N3: Part2.D9_PWM, J4.pulse
  N4: Part2.D2, S1.Pin_1, S1.Pin_2, R3.Pin_0
  N5: Part2.D4, S2.Pin_1, S2.Pin_2, R4.Pin_1
  5V: Part2.5V, J4.vcc, S1.Pin_3, S1.Pin_4, R1.leg2, S2.Pin_3, S2.Pin_4, VCC1.+
  N6: R1.leg1, R3.Pin_1, R4.Pin_0, VCC1.-
